# Fritzing sketch reset (saved by Fritzing 0.9.3b)

parts:
  LED_Alarm = LED - 5mm [color="Red (633nm)" package="5 mm [THT]"]
  R1 = Resistor [tolerance=±5% resistance=220 package=THT]
  WeMos_D1_Mini1 = WeMos D1 Mini
  Relay = WeMos D1 Mini Relay Shield V2
  config = Pushbutton [package="[THT]"]
  F1 = FUSE [package=fuse_5mm]  # not connected

nets:
  N1: LED_Alarm.cathode, WeMos_D1_Mini1.D1
  N2: R1.Pin_0, WeMos_D1_Mini1.G, Relay.G
  5V: WeMos_D1_Mini1.5V, Relay.5V
  N3: WeMos_D1_Mini1.D2, Relay.D2
  N4: WeMos_D1_Mini1.D3, config.Pin_2

notes:
  220v in
  220v out
