# Fritzing sketch resetV4 (saved by Fritzing 0.9.3b)

parts:
  WeMos_D1_Mini1 = WeMos D1 Mini
  config = Pushbutton [package="[THT]"]
  Fuse = FUSE [package=fuse_5mm]  # not connected
  S_+_- = KY-019 5V Relay Module [package="Breakout board"]

nets:
  N1: WeMos_D1_Mini1.5V, S_+_-.+
  N2: WeMos_D1_Mini1.D2, S_+_-.S
  N3: WeMos_D1_Mini1.D3, config.Pin_2
  N4: WeMos_D1_Mini1.G, config.Pin_3, config.Pin_4, S_+_-.-

notes:
  220v in
  220v out

custom parts:
  KY-019 5V Relay Module: KY-019 5V Relay module, used to control AC circuits.
